# Fritzing sketch z-axes-connectors (saved by Fritzing 0.9.3b)
stripboards: 2

parts:
  J2 = female pin header, 4 pins [form="♀ (female)"]
  Power_plug1 = Power plug
  J3 = female pin header, 2 pins [form="♀ (female)"]
  J4 = female pin header, 4 pins [form="♀ (female)"]
  J5 = female pin header, 2 pins [form="♀ (female)"]
  J7 = female pin header, 4 pins [form="♀ (female)"]
  J8 = female pin header, 4 pins [form="♀ (female)"]
  J9 = female pin header, 2 pins [form="♀ (female)"]
  J10 = female pin header, 2 pins [form="♀ (female)"]
  J11 = female pin header, 3 pins [form="♀ (female)"]
  J12 = female pin header, 3 pins [form="♀ (female)"]
  J13 = female pin header, 5 pins [form="♀ (female)"]
  J14 = female pin header, 2 pins [form="♀ (female)"]
  J15 = female pin header, 2 pins [form="♀ (female)"]
  J16 = female pin header, 5 pins [form="♀ (female)"]
  J6 = female pin header, 1 pin [form="♀ (female)"]

nets:
  N1: J2.pin1, J13.pin3, J16.pin3
  N2: J2.pin2, J3.pin1, J4.pin2
  N3: J2.pin3, J3.pin2, J4.pin3
  N4: J2.pin4, Power_plug1.VCC, J4.pin4
  N5: J4.pin1, J5.pin1, J6.pin1
  N6: J5.pin2, J13.pin4, J16.pin4
  N7: J7.pin1, J8.pin1
  N8: J7.pin2, J8.pin2
  N9: J7.pin3, J8.pin3
  N10: J7.pin4, J8.pin4
  N11: J9.pin1, J10.pin1, J11.pin1, J12.pin1
  N12: J9.pin2, J10.pin2, J11.pin2, J12.pin2
  N13: J11.pin3, J12.pin3, J13.pin2, J16.pin2
  N14: J13.pin1, J15.pin1, J16.pin1
  N15: J13.pin5, J14.pin2, J16.pin5
  N16: J14.pin1, J15.pin2

notes:
  Motor Out
  SCL/SDA
  TOF
  5V
  Air
  AIR
  D10
  Spindle
  Laser
  +
  -
  PWM
  SW1
  SW2
